// Logisim project CS23B1047_assign.circ as structural Verilog: 1 circuit, main circuit main
module main (
  input  RESET
);

  wire and_1_out, and_2_out, and_3_out, and_4_out, and_5_out, and_6_out, and_7_out, and_8_out, and_9_out,
       and_10_out, and_11_out, and_12_out, CLK_out, not_1_out, not_2_out, not_3_out, not_4_out, or_1_out,
       or_2_out, or_3_out, or_4_out, or_5_out, or_6_out, or_7_out, or_8_out, TA_q, TA_qn, TB_q, TC_q, TD_q;

  Clock CLK (.out(CLK_out));
  T_Flip_Flop TD (.T(TA_qn), .clk(CLK_out), .Q(TD_q), .reset(RESET));  // open: Qn, preset
  T_Flip_Flop TC (.T(TD_q), .clk(CLK_out), .Q(TC_q), .reset(RESET));  // open: Qn, preset
  not not_1 (not_1_out, TD_q);
  and and_1 (and_1_out, TD_q, TC_q);
  not not_2 (not_2_out, TC_q);
  T_Flip_Flop TB (.T(and_1_out), .clk(CLK_out), .Q(TB_q), .reset(RESET));  // open: Qn, preset
  and and_2 (and_2_out, TC_q, TD_q);
  or or_1 (or_1_out, TC_q, TD_q);
  and and_3 (and_3_out, and_1_out, TB_q);
  not not_3 (not_3_out, TB_q);
  or or_2 (or_2_out, and_3_out, TA_q);
  and and_4 (and_4_out, TC_q, not_1_out);
  and and_5 (and_5_out, TB_q, TD_q);
  and and_6 (and_6_out, TB_q, not_1_out);
  and and_7 (and_7_out, TB_q, TC_q);
  and and_8 (and_8_out, not_2_out, not_1_out, TB_q);
  and and_9 (and_9_out, not_3_out, or_1_out);
  T_Flip_Flop TA (.T(or_2_out), .clk(CLK_out), .Q(TA_q), .Qn(TA_qn), .reset(RESET));  // open: preset
  not not_4 (not_4_out, TA_q);
  and and_10 (and_10_out, not_4_out, not_3_out);
  and and_11 (and_11_out, not_4_out, not_1_out);
  and and_12 (and_12_out, not_4_out, not_2_out, not_3_out);
  or or_3 (or_3_out, and_10_out, and_11_out);
  or or_4 (or_4_out, TA_q, not_3_out, and_4_out);
  or or_5 (or_5_out, TA_q, and_5_out, TC_q);
  or or_6 (or_6_out, TB_q, TD_q, TA_q);
  or or_7 (or_7_out, and_6_out, and_7_out, and_12_out);
  or or_8 (or_8_out, and_8_out, and_2_out, and_9_out);
  _7_Segment_Display u_7_segment_display_1 (
    .g(or_8_out), .f(or_7_out), .a(or_4_out), .b(or_5_out), .e(and_11_out), .d(or_3_out), .c(or_6_out));  // open: dp

  // Notes on the sheet:
  //   Q0
  //   Q0
  //   Q'0
  //   Q1
  //   Q1
  //   Q'1
  //   Q2
  //   Q2
  //   Q'2
  //   Q3
  //   Q3
  //   Q'3
  //   Q'3
  //   a
  //   b
  //   c
  //   d
  //   e
  //   f
  //   g
endmodule
