// Logisim project UNIVERSALSHIFT.circ as structural Verilog: 1 circuit, main circuit main
module main (
  input  I0,
  input  I1,
  input  I2,
  input  I3,
  input  Right,
  input  Left,
  input  in_7,
  input  in_8,
  output out_9,
  output out_10,
  output out_11,
  output out_12
);

  wire clk_out, multiplexer_1_out, multiplexer_2_out, multiplexer_3_out, multiplexer_4_out;

  Clock clk (.out(clk_out));
  D_Flip_Flop #(.trigger("falling")) d_ff_1 (
    .D(multiplexer_1_out), .clk(clk_out), .Q(out_9));  // open: Qn, preset, reset
  Multiplexer #(.select(2)) multiplexer_1 (
    .in0(Right), .in1(out_10), .in2(I0), .in3(out_9), .out(multiplexer_1_out), .sel({in_8, in_7}));
  Multiplexer #(.select(2)) multiplexer_2 (
    .in0(out_9), .in1(out_11), .in2(I1), .in3(out_10), .out(multiplexer_2_out), .sel({in_8, in_7}));
  D_Flip_Flop #(.trigger("falling")) d_ff_2 (
    .D(multiplexer_2_out), .clk(clk_out), .Q(out_10));  // open: Qn, preset, reset
  Multiplexer #(.select(2)) multiplexer_3 (
    .in0(out_10), .in1(out_12), .in2(I2), .in3(out_11), .out(multiplexer_3_out), .sel({in_8, in_7}));
  D_Flip_Flop #(.trigger("falling")) d_ff_3 (
    .D(multiplexer_3_out), .clk(clk_out), .Q(out_11));  // open: Qn, preset, reset
  Multiplexer #(.select(2)) multiplexer_4 (
    .in0(out_11), .in1(Left), .in2(I3), .in3(out_12), .out(multiplexer_4_out), .sel({in_8, in_7}));
  D_Flip_Flop #(.trigger("falling")) d_ff_4 (
    .D(multiplexer_4_out), .clk(clk_out), .Q(out_12));  // open: Qn, preset, reset
endmodule
